// Logisim project TME1.circ as structural Verilog: 6 circuits, main circuit MUX2
module MUX2 (
  input  v,
  input  e0,
  input  e1,
  output out_4
);

  wire and_1_out, and_2_out, not_1_out;

  not not_1 (not_1_out, v);
  and and_1 (and_1_out, not_1_out, e0);
  and and_2 (and_2_out, v, e1);
  or or_1 (out_4, and_1_out, and_2_out);
endmodule

module mux2sur4 (
  input  i,
  input  a3,
  input  b3,
  input  a2,
  input  b2,
  input  a1,
  input  b1,
  input  a0,
  input  b0,
  output s3,
  output s2,
  output s1,
  output s0
);

  MUX2 mux2_1 (.e0(a3), .e1(b3), .v(i), .out_4(s3));
  MUX2 mux2_2 (.e0(a2), .e1(b2), .v(i), .out_4(s2));
  MUX2 mux2_3 (.e0(a1), .e1(b1), .v(i), .out_4(s1));
  MUX2 mux2_4 (.e0(a0), .e1(b0), .v(i), .out_4(s0));
endmodule

module mon_xor (
  input  in_1,
  input  in_2,
  output out_3
);

  wire and_1_out, and_2_out, not_1_out, not_2_out;

  not not_1 (not_1_out, in_1);
  not not_2 (not_2_out, in_2);
  and and_1 (and_1_out, not_1_out, in_2);
  and and_2 (and_2_out, in_1, not_2_out);
  or or_1 (out_3, and_1_out, and_2_out);
endmodule

module mux4vers1_beta (
  input  i1,
  input  i0,
  input  e3,
  input  e2,
  input  e1,
  input  e0,
  output out_7
);

  wire and_1_out, and_2_out, and_3_out, and_4_out, not_1_out, not_2_out;

  not not_1 (not_1_out, i1);
  not not_2 (not_2_out, i0);
  and and_1 (and_1_out, not_2_out, not_1_out, e3);
  and and_2 (and_2_out, not_1_out, i0, e2);
  and and_3 (and_3_out, i1, not_2_out, e1);
  and and_4 (and_4_out, i0, i1, e0);
  or or_1 (out_7, and_1_out, and_2_out, and_3_out, and_4_out);
endmodule

module ETNON (
  input  a,
  input  b,
  output out_3
);

  wire not_1_out;

  not not_1 (not_1_out, b);
  and and_1 (out_3, a, not_1_out);
endmodule

module mux4vers1 (
  input  i1,
  input  i0,
  input  e3,
  input  e2,
  input  e1,
  input  e0,
  output s
);

  wire mux2_1_out_4, mux2_2_out_4;

  MUX2 mux2_1 (.e0(e3), .e1(e2), .v(i1), .out_4(mux2_1_out_4));
  MUX2 mux2_2 (.e0(e1), .e1(e0), .v(i1), .out_4(mux2_2_out_4));
  MUX2 mux2_3 (.e0(mux2_1_out_4), .e1(mux2_2_out_4), .v(i0), .out_4(s));
endmodule
