// Logisim project TME2.circ as structural Verilog: 6 circuits, main circuit Add_red
module Add_red (
  input  cin,
  input  a,
  input  b,
  output s,
  output cout
);

  wire and_1_out, and_2_out, xor_2_out;

  xor xor_1 (s, a, b, cin);
  and and_1 (and_1_out, b, cin);
  xor xor_2 (xor_2_out, b, cin);
  and and_2 (and_2_out, a, xor_2_out);
  or or_1 (cout, and_2_out, and_1_out);
endmodule

module Addinion (
  input  cin,
  input  a,
  input  b,
  output s,
  output cout
);

  wire and_1_out, and_2_out, and_3_out, and_4_out, and_5_out, and_6_out, and_7_out, not_1_out, not_2_out,
       not_3_out;

  not not_1 (not_1_out, a);
  not not_2 (not_2_out, b);
  not not_3 (not_3_out, cin);
  and and_1 (and_1_out, not_1_out, not_2_out, cin);
  and and_2 (and_2_out, not_1_out, b, not_3_out);
  and and_3 (and_3_out, a, not_2_out, not_3_out);
  and and_4 (and_4_out, a, b, cin);
  and and_5 (and_5_out, cin, not_1_out, b);
  and and_6 (and_6_out, a, not_2_out, cin);
  and and_7 (and_7_out, b, a, not_3_out);
  or or_1 (s, and_1_out, and_2_out, and_3_out, and_4_out);
  or or_2 (cout, and_4_out, and_5_out, and_6_out, and_7_out);
endmodule

// Addit
module Add4bits (
  input  cin,
  input  a3,
  input  b3,
  input  a2,
  input  b2,
  input  a1,
  input  b1,
  input  a0,
  input  b0,
  output s3,
  output s2,
  output s1,
  output s0,
  output cout
);

  wire add_red_1_cout, add_red_2_cout, add_red_3_cout;

  Add_red add_red_1 (.a(a3), .b(b3), .cin(cin), .cout(add_red_1_cout), .s(s3));
  Add_red add_red_2 (.a(a2), .b(b2), .cin(add_red_1_cout), .cout(add_red_2_cout), .s(s2));
  Add_red add_red_3 (.a(a1), .b(b1), .cin(add_red_2_cout), .cout(add_red_3_cout), .s(s1));
  Add_red add_red_4 (.a(a0), .b(b0), .cin(add_red_3_cout), .cout(cout), .s(s0));
endmodule

module Soustracteur (
  input  bin,
  input  a,
  input  b,
  output d,
  output bout
);

  wire and_1_out, and_2_out, not_1_out, xor_2_out;

  not not_1 (not_1_out, a);
  xor xor_1 (d, bin, a, b);
  and and_1 (and_1_out, bin, b);
  xor xor_2 (xor_2_out, bin, b);
  or or_1 (bout, and_1_out, and_2_out);
  and and_2 (and_2_out, xor_2_out, not_1_out);
endmodule

// Soustrac
module Sous4bits (
  input  bin,
  input  a3,
  input  b3,
  input  a2,
  input  b2,
  input  a1,
  input  b1,
  input  a0,
  input  b0,
  output s3,
  output s2,
  output s1,
  output s0,
  output bout
);

  wire soustracteur_1_bout, soustracteur_2_bout, soustracteur_3_bout;

  Soustracteur soustracteur_1 (.a(a3), .b(b3), .bin(bin), .bout(soustracteur_1_bout), .d(s3));
  Soustracteur soustracteur_2 (.a(a2), .b(b2), .bin(soustracteur_1_bout), .bout(soustracteur_2_bout), .d(s2));
  Soustracteur soustracteur_3 (.a(a1), .b(b1), .bin(soustracteur_2_bout), .bout(soustracteur_3_bout), .d(s1));
  Soustracteur soustracteur_4 (.a(a0), .b(b0), .bin(soustracteur_3_bout), .bout(bout), .d(s0));
endmodule

module Add_sous (
  input  cin,
  input  a3,
  input  b3,
  input  Add_Sous,
  input  a2,
  input  b2,
  input  bin,
  input  a1,
  input  b1,
  input  a0,
  input  b0,
  output s3,
  output s2,
  output s1,
  output s0,
  output CY
);

  wire [4:0] add4bits_1_s3, sous4bits_1_s3;

  Add4bits add4bits_1 (
    .a3(a3), .b3(b3), .a2(a2), .b2(b2), .a1(a1), .b1(b1), .a0(a0), .b0(b0), .cin(cin), .s3(add4bits_1_s3[0]),
    .s2(add4bits_1_s3[1]), .s1(add4bits_1_s3[2]), .s0(add4bits_1_s3[3]), .cout(add4bits_1_s3[4]));
  Sous4bits sous4bits_1 (
    .a3(a3), .b3(b3), .a2(a2), .b2(b2), .a1(a1), .b1(b1), .a0(a0), .b0(b0), .bin(bin),
    .s3(sous4bits_1_s3[0]), .s2(sous4bits_1_s3[1]), .s1(sous4bits_1_s3[2]), .s0(sous4bits_1_s3[3]),
    .bout(sous4bits_1_s3[4]));
  Multiplexer #(.width(5), .enable("false")) multiplexer_1 (
    .in0(add4bits_1_s3), .in1(sous4bits_1_s3), .out({CY, s0, s1, s2, s3}), .sel(Add_Sous));
endmodule
