// Logisim project TME3.circ as structural Verilog: 5 circuits, main circuit ALU
module ALU (
  input  Aluop,
  input  X3,
  input  X2,
  input  X1,
  input  X0,
  input  Y3,
  input  Y2,
  input  Y1,
  input  Y0,
  output S3,
  output S2,
  output S1,
  output S0,
  output cout
);

  wire [3:0] multiplexer_1_out, not_1_out;

  assign not_1_out = ~{Y0, Y1, Y2, Y3};  // NOT_Gate not_1, 4 bits wide
  Multiplexer #(.width(4), .enable("false")) multiplexer_1 (
    .in0({Y0, Y1, Y2, Y3}), .in1(not_1_out), .out(multiplexer_1_out), .sel(Aluop));
  Add4bits add4bits_1 (
    .a3(X3), .b3(multiplexer_1_out[0]), .a2(X2), .b2(multiplexer_1_out[1]), .a1(X1),
    .b1(multiplexer_1_out[2]), .a0(X0), .b0(multiplexer_1_out[3]), .cin(Aluop), .s3(S3), .s2(S2), .s1(S1),
    .s0(S0), .cout(cout));
endmodule

module ALU_flags (
  input  Aluop,
  input  [3:0] A,
  input  [3:0] B,
  output [3:0] out_4,
  output CF,
  output OV,
  output ZF,
  output SF
);

  wire add_red_1_cout, add_red_2_cout, add_red_3_cout, or_1_out;
  wire [3:0] multiplexer_1_out, not_1_out;

  assign not_1_out = ~B;  // NOT_Gate not_1, 4 bits wide
  Multiplexer #(.width(4), .enable("false")) multiplexer_1 (
    .in0(B), .in1(not_1_out), .out(multiplexer_1_out), .sel(Aluop));
  Add_red add_red_1 (.a(A[0]), .b(multiplexer_1_out[0]), .cin(Aluop), .cout(add_red_1_cout), .s(out_4[0]));
  Add_red add_red_2 (.a(A[1]), .b(multiplexer_1_out[1]), .cin(add_red_1_cout), .cout(add_red_2_cout), .s(out_4[1]));
  Add_red add_red_3 (.a(A[2]), .b(multiplexer_1_out[2]), .cin(add_red_2_cout), .cout(add_red_3_cout), .s(out_4[2]));
  Addinion addinion_1 (.a(A[3]), .b(multiplexer_1_out[3]), .cin(add_red_3_cout), .cout(CF), .s(out_4[3]));
  xor xor_1 (OV, CF, add_red_3_cout);
  not not_2 (ZF, or_1_out);
  or or_1 (or_1_out, out_4[0], out_4[1], out_4[2], out_4[3]);

  assign SF = out_4[3];
endmodule

module SHR (
  input  x3,
  input  x2,
  input  x1,
  input  x0,
  input  d1,
  input  d0,
  output s3,
  output s2,
  output s1,
  output s0
);

  wire and_1_out, and_2_out, and_3_out, multiplexer_1_out, not_1_out, not_2_out, or_1_out;

  or or_1 (or_1_out, d0, d1);
  and and_1 (and_1_out, x3, or_1_out);
  Multiplexer #(.enable("false")) multiplexer_1 (.in0(x1), .in1(x2), .out(multiplexer_1_out), .sel(d0));
  and and_2 (and_2_out, not_1_out, not_2_out);
  not not_1 (not_1_out, d1);
  not not_2 (not_2_out, d0);
  and and_3 (and_3_out, x2, and_2_out);
  Multiplexer #(.enable("false")) multiplexer_2 (.in0(multiplexer_1_out), .in1(x3), .out(s1), .sel(d1));
  or or_2 (s2, and_3_out, and_1_out);
  Multiplexer #(.select(2), .enable("false")) multiplexer_3 (
    .in0(x0), .in1(x1), .in2(x2), .in3(x3), .out(s0), .sel({d1, d0}));

  assign s3 = x3;
endmodule

module SHL (
  input  x3,
  input  x2,
  input  x1,
  input  x0,
  input  d1,
  input  d0,
  output s3,
  output s2,
  output s1,
  output s0
);

  wire and_1_out, multiplexer_1_out, multiplexer_3_out, not_1_out, not_2_out, not_3_out, not_4_out;

  not not_1 (not_1_out, d0);
  and and_1 (and_1_out, x0, not_1_out);
  not not_2 (not_2_out, d1);
  not not_3 (not_3_out, d0);
  Multiplexer #(.enable("false")) multiplexer_1 (.in0(x2), .in1(x1), .out(multiplexer_1_out), .sel(d0));
  and and_2 (s0, x0, not_2_out, not_3_out);
  Multiplexer #(.select(2), .enable("false")) multiplexer_2 (
    .in0(x3), .in1(x2), .in2(x1), .in3(x0), .out(s3), .sel({d1, d0}));
  Multiplexer #(.enable("false")) multiplexer_3 (.in0(x1), .in1(x0), .out(multiplexer_3_out), .sel(d0));
  Multiplexer #(.enable("false")) multiplexer_4 (.in0(multiplexer_1_out), .in1(and_1_out), .out(s2), .sel(d1));
  not not_4 (not_4_out, d1);
  and and_3 (s1, multiplexer_3_out, not_4_out);
endmodule

module CMP (
  input  a3,
  input  a2,
  input  a1,
  input  a0,
  input  b3,
  input  b2,
  input  b1,
  input  b0,
  output S
);

  wire and_1_out, and_2_out, and_3_out, and_4_out, and_5_out, and_6_out, and_7_out, not_1_out, not_2_out,
       not_3_out, not_4_out, or_1_out, or_2_out, xnor_1_out, xnor_2_out, xnor_3_out;

  not not_1 (not_1_out, a3);
  not not_2 (not_2_out, a2);
  not not_3 (not_3_out, a1);
  not not_4 (not_4_out, a0);
  and and_1 (and_1_out, not_1_out, b3);
  and and_2 (and_2_out, not_2_out, b2);
  and and_3 (and_3_out, not_3_out, b1);
  and and_4 (and_4_out, not_4_out, b0);
  xnor xnor_1 (xnor_1_out, a1, b1);
  and and_5 (and_5_out, and_4_out, xnor_1_out);
  xnor xnor_2 (xnor_2_out, a2, b2);
  xnor xnor_3 (xnor_3_out, a3, b3);
  or or_1 (or_1_out, and_3_out, and_5_out);
  or or_2 (or_2_out, and_2_out, and_6_out);
  and and_6 (and_6_out, or_1_out, xnor_2_out);
  and and_7 (and_7_out, or_2_out, xnor_3_out);
  or or_3 (S, and_1_out, and_7_out);
endmodule
