// Logisim project TME4.circ as structural Verilog: 5 circuits, main circuit REG1bit
module REG1bit (
  input  Din,
  input  WE,
  output Dout
);

  wire clock_1_out;

  Register #(.width(1)) register_1 (.D(Din), .en(WE), .Q(Dout), .clk(clock_1_out), .clr(1'b0));
  Clock clock_1 (.out(clock_1_out));
endmodule

module REG4bits (
  input  [3:0] Din,
  input  WE,
  output [3:0] Dout
);

  wire CK_out;

  Register #(.width(4)) register_1 (.D(Din), .en(WE), .Q(Dout), .clk(CK_out), .clr(1'b0));
  Clock CK (.out(CK_out));
endmodule

module _4REG_ALU (
  input  [3:0] Din_A,
  input  Add_Sub,
  input  WE_A,
  input  ext_A,
  input  [3:0] Din_B,
  input  WE_B,
  input  [1:0] in_7,
  input  ext_B,
  input  [3:0] Din_C,
  input  WE_C,
  input  ext_C,
  input  [3:0] Din_D,
  input  WE_D,
  input  ext_D,
  input  [1:0] in_15,
  output CF,
  output OV,
  output ZF,
  output SF
);

  wire CK_out;
  wire [3:0] alu_flags_1_out_4, multiplexer_1_out, multiplexer_2_out, multiplexer_3_out, multiplexer_4_out,
       multiplexer_5_out, multiplexer_6_out, RA_q, RB_q, RC_q, RD_q;

  Multiplexer #(.width(4), .enable("false")) multiplexer_1 (
    .in0(alu_flags_1_out_4), .in1(Din_A), .out(multiplexer_1_out), .sel(ext_A));
  Multiplexer #(.width(4), .enable("false")) multiplexer_2 (
    .in0(alu_flags_1_out_4), .in1(Din_B), .out(multiplexer_2_out), .sel(ext_B));
  Multiplexer #(.width(4), .enable("false")) multiplexer_3 (
    .in0(alu_flags_1_out_4), .in1(Din_C), .out(multiplexer_3_out), .sel(ext_C));
  Multiplexer #(.width(4), .enable("false")) multiplexer_4 (
    .in0(alu_flags_1_out_4), .in1(Din_D), .out(multiplexer_4_out), .sel(ext_D));
  Clock CK (.out(CK_out));
  Register #(.width(4)) RA (.D(multiplexer_1_out), .en(WE_A), .Q(RA_q), .clk(CK_out), .clr(1'b0));
  Register #(.width(4)) RB (.D(multiplexer_2_out), .en(WE_B), .Q(RB_q), .clk(CK_out), .clr(1'b0));
  Register #(.width(4)) RC (.D(multiplexer_3_out), .en(WE_C), .Q(RC_q), .clk(CK_out), .clr(1'b0));
  Register #(.width(4)) RD (.D(multiplexer_4_out), .en(WE_D), .Q(RD_q), .clk(CK_out), .clr(1'b0));
  Multiplexer #(.select(2), .width(4), .enable("false")) multiplexer_5 (
    .in0(RA_q), .in1(RB_q), .in2(RC_q), .in3(RD_q), .out(multiplexer_5_out), .sel(in_7));
  Multiplexer #(.select(2), .width(4), .enable("false")) multiplexer_6 (
    .in0(RA_q), .in1(RB_q), .in2(RC_q), .in3(RD_q), .out(multiplexer_6_out), .sel(in_15));
  ALU_flags alu_flags_1 (
    .A(multiplexer_5_out), .B(multiplexer_6_out), .Aluop(Add_Sub), .out_4(alu_flags_1_out_4), .CF(CF),
    .OV(OV), .ZF(ZF), .SF(SF));
endmodule

module Mem16sur8bits (
  input  [3:0] ADR,
  input  [7:0] DATA_in,
  input  Clear,
  input  C_S,
  input  CMD,
  output [7:0] DATA_out
);

  wire CK_out, not_1_out;

  Clock CK (.out(CK_out));
  not not_1 (not_1_out, CMD);
  RAM #(.addrWidth(4), .bus("separate")) ram_1 (
    .addr(ADR), .din(DATA_in), .data(DATA_out), .str(CMD), .sel(C_S), .clk(CK_out), .ld(not_1_out),
    .clr(Clear));
endmodule

module Mem8sur16bits (
  input  [2:0] ADR,
  input  Clear,
  input  [31:0] DATA_in,
  input  C_S,
  input  CMD,
  output [31:0] DATA_out
);

  wire CK_out, not_1_out;

  Clock CK (.out(CK_out));
  not not_1 (not_1_out, CMD);
  RAM #(.addrWidth(3), .dataWidth(32), .bus("separate")) ram_1 (
    .addr(ADR), .din(DATA_in), .data(DATA_out), .str(CMD), .sel(C_S), .clk(CK_out), .ld(not_1_out),
    .clr(Clear));
endmodule
