// Logisim project TME5.circ as structural Verilog: 4 circuits, main circuit main
module main (
  input  CteOutputXEnable,
  input  RegOutputXEnable,
  input  ADOutputXEnable,
  input  DTOutputXEnable,
  input  RegWriteEnable,
  input  ADWriteEnable,
  input  DTWriteEnable,
  input  [1:0] NumRegToRead,
  input  [1:0] NumRegToWrite,
  input  [3:0] Constante,
  input  CteOutputYEnable,
  input  ADOutputYEnable,
  input  DTOutputYEnable,
  input  ADOutputAddressEnable,
  input  clock,
  input  StoreCommand,
  input  LoadCommand,
  output [3:0] ValeurSurDataIn,
  output [3:0] ValeurSurBusX,
  output [3:0] ValeurSurResOut_DataOut,
  output [3:0] ValeurSurBusY,
  output [3:0] ValeurSurBusAdresse
);

  wire [3:0] AD_q, banc_registre_1_readvalue, controlled_buffer_4_out, DT_q;

  assign ValeurSurBusX = CteOutputXEnable ? Constante : 4'bz;  // Controlled_Buffer controlled_buffer_1
  assign ValeurSurBusY = CteOutputYEnable ? Constante : 4'bz;  // Controlled_Buffer controlled_buffer_2
  assign ValeurSurBusX = RegOutputXEnable ? banc_registre_1_readvalue : 4'bz;  // Controlled_Buffer controlled_buffer_3
  assign controlled_buffer_4_out = RegWriteEnable ? ValeurSurResOut_DataOut : 4'bz;  // Controlled_Buffer controlled_buffer_4
  banc_registre banc_registre_1 (
    .NumReadReg(NumRegToRead), .NumWriteReg(NumRegToWrite), .ValueToWrite(controlled_buffer_4_out),
    .Clock(clock), .ReadValue(banc_registre_1_readvalue));
  assign ValeurSurBusX = ADOutputXEnable ? AD_q : 4'bz;  // Controlled_Buffer controlled_buffer_5
  Register #(.width(4)) AD (.D(ValeurSurResOut_DataOut), .en(ADWriteEnable), .Q(AD_q), .clk(clock), .clr(1'b0));
  assign ValeurSurBusAdresse = ADOutputAddressEnable ? AD_q : 4'bz;  // Controlled_Buffer controlled_buffer_6
  assign ValeurSurBusY = ADOutputYEnable ? AD_q : 4'bz;  // Controlled_Buffer controlled_buffer_7
  assign ValeurSurBusX = DTOutputXEnable ? DT_q : 4'bz;  // Controlled_Buffer controlled_buffer_8
  Register #(.width(4)) DT (.D(ValeurSurDataIn), .en(DTWriteEnable), .Q(DT_q), .clk(clock), .clr(1'b0));
  assign ValeurSurBusY = DTOutputYEnable ? DT_q : 4'bz;  // Controlled_Buffer controlled_buffer_9
  Adder #(.width(4)) adder_1 (
    .a(ValeurSurBusX), .b(ValeurSurBusY), .out(ValeurSurResOut_DataOut), .cin(1'b0));  // open: cout
  RAM #(.addrWidth(4), .dataWidth(4), .bus("separate")) ram_1 (
    .addr(ValeurSurBusAdresse), .din(ValeurSurResOut_DataOut), .data(ValeurSurDataIn), .str(StoreCommand),
    .sel(1'b1), .clk(clock), .ld(LoadCommand));  // open: clr

  // Notes on the sheet:
  //   bloc de constantes 4 bits
  //   bus X
  //   bus Y
  //   banc de 4 registres
  //   4 bits
  //   bus ADRESSE
  //   DATA_IN
  //   RES_OUT
  //   ADD
endmodule

// Banc
module banc_registre (
  input  [3:0] ValueToWrite,
  input  [1:0] NumReadReg,
  input  [1:0] NumWriteReg,
  input  Clock,
  output [3:0] ReadValue
);

  wire decoder_1_out0, decoder_1_out1, decoder_1_out2, decoder_1_out3;
  wire [3:0] R0_q, R1_q, R2_q, R3_q;

  Decoder #(.select(2)) decoder_1 (
    .out0(decoder_1_out0), .out1(decoder_1_out1), .out2(decoder_1_out2), .out3(decoder_1_out3),
    .sel(NumWriteReg), .en(1'b1));
  Register #(.width(4)) R0 (.D(4'b0000), .en(decoder_1_out0), .Q(R0_q), .clk(Clock), .clr(1'b0));
  Register #(.width(4)) R1 (.D(ValueToWrite), .en(decoder_1_out1), .Q(R1_q), .clk(Clock), .clr(1'b0));
  Register #(.width(4)) R2 (.D(ValueToWrite), .en(decoder_1_out2), .Q(R2_q), .clk(Clock), .clr(1'b0));
  Register #(.width(4)) R3 (.D(ValueToWrite), .en(decoder_1_out3), .Q(R3_q), .clk(Clock), .clr(1'b0));
  Multiplexer #(.select(2), .width(4)) multiplexer_1 (
    .in0(R0_q), .in1(R1_q), .in2(R2_q), .in3(R3_q), .out(ReadValue), .sel(NumReadReg));  // open: en
endmodule

module Mem16sur8bits (
  input  [3:0] ADR,
  input  [7:0] DATA_in,
  input  Clear,
  input  C_S,
  input  CMD,
  output [7:0] DATA_out
);

  wire CK_out, not_1_out;

  Clock CK (.out(CK_out));
  not not_1 (not_1_out, CMD);
  RAM #(.addrWidth(4), .bus("separate")) ram_1 (
    .addr(ADR), .din(DATA_in), .data(DATA_out), .str(CMD), .sel(C_S), .clk(CK_out), .ld(not_1_out),
    .clr(Clear));
endmodule

module Mem8sur16bits (
  input  [2:0] ADR,
  input  Clear,
  input  [31:0] DATA_in,
  input  C_S,
  input  CMD,
  output [31:0] DATA_out
);

  wire CK_out, not_1_out;

  Clock CK (.out(CK_out));
  not not_1 (not_1_out, CMD);
  RAM #(.addrWidth(3), .dataWidth(32), .bus("separate")) ram_1 (
    .addr(ADR), .din(DATA_in), .data(DATA_out), .str(CMD), .sel(C_S), .clk(CK_out), .ld(not_1_out),
    .clr(Clear));
endmodule
